# Fritzing sketch schema-di-montaggio (saved by Fritzing 0.9.9b)
breadboards: 2

parts:
  Disp3 = 60mm 8x8 dot matrix column cathode led display with narrow pcb pads
  Componente1 = Arduino Uno (Rev3)

nets:
  N1: Disp3.pin_1, Componente1.D4
  N2: Disp3.pin_2, Componente1.D11_PWM/MOSI
  N3: Disp3.pin_3, Componente1.D12/MISO
  N4: Disp3.pin_4, Componente1.D7
  N5: Disp3.pin_5, Componente1.A0
  N6: Disp3.pin_6, Componente1.D2
  N7: Disp3.pin_7, Componente1.D10_PWM/SS
  N8: Disp3.pin_8, Componente1.D3_PWM
  N9: Disp3.pin_9, Componente1.A3
  N10: Disp3.pin_10, Componente1.D13/SCK
  N11: Disp3.pin_11, Componente1.D6_PWM
  N12: Disp3.pin_12, Componente1.D8
  N13: Disp3.pin_13, Componente1.D9_PWM
  N14: Disp3.pin_14, Componente1.A2
  N15: Disp3.pin_15, Componente1.A1
  N16: Disp3.pin_16, Componente1.D5_PWM
