# Fritzing sketch schema-montaggio (saved by Fritzing 0.9.10b)
breadboards: 1

parts:
  Componente1 = Arduino Uno (Rev3) - ICSP
  R1 = Resistor [tolerance=±5% power=0.25 resistance=220 package=THT]
  LED1 = LED - 5mm [color="Blue (430nm)" current=0.030 package="5 mm [THT]"]
  R2 = Rotary Potentiometer (Small) [maximum_resistance=100kΩ knob_status=50% power=0.5W package=THT]
  LED2 = LED - 5mm [color="Blue (430nm)" current=0.030 package="5 mm [THT]"]
  LED3 = LED - 5mm [color="Blue (430nm)" current=0.030 package="5 mm [THT]"]
  LED4 = LED - 5mm [color="Blue (430nm)" current=0.030 package="5 mm [THT]"]
  LED5 = LED - 5mm [color="Blue (430nm)" current=0.030 package="5 mm [THT]"]
  LED6 = LED - 5mm [color="Blue (430nm)" current=0.030 package="5 mm [THT]"]
  LED7 = LED - 5mm [color="Blue (430nm)" current=0.030 package="5 mm [THT]"]
  LED8 = LED - 5mm [color="Blue (430nm)" current=0.030 package="5 mm [THT]"]
  LED9 = LED - 5mm [color="Blue (430nm)" current=0.030 package="5 mm [THT]"]
  LED10 = LED - 5mm [color="Blue (430nm)" current=0.030 package="5 mm [THT]"]
  R3 = Resistor [tolerance=±5% power=0.25 resistance=220 package=THT]
  R4 = Resistor [tolerance=±5% power=0.25 resistance=220 package=THT]
  R5 = Resistor [tolerance=±5% power=0.25 resistance=220 package=THT]
  R6 = Resistor [tolerance=±5% power=0.25 resistance=220 package=THT]
  R7 = Resistor [tolerance=±5% power=0.25 resistance=220 package=THT]
  R8 = Resistor [tolerance=±5% power=0.25 resistance=220 package=THT]
  R9 = Resistor [tolerance=±5% power=0.25 resistance=220 package=THT]
  R10 = Resistor [tolerance=±5% power=0.25 resistance=220 package=THT]
  R11 = Resistor [tolerance=±5% power=0.25 resistance=220 package=THT]

nets:
  N1: Componente1.A0, R2.wiper
  N2: Componente1.GND, R1.Pin_1, R2.leg1, R3.Pin_1, R4.Pin_1, R5.Pin_1, R6.Pin_1, R7.Pin_1, R8.Pin_1, R9.Pin_1, R10.Pin_1, R11.Pin_1
  N3: Componente1.D8, LED7.anode
  N4: Componente1.D9_PWM, LED8.anode
  N5: Componente1.D10_PWM/SS, LED9.anode
  N6: Componente1.D11_PWM/MOSI, LED10.anode
  N7: Componente1.D2, LED1.anode
  N8: Componente1.D3_PWM, LED2.anode
  N9: Componente1.D4, LED3.anode
  N10: Componente1.D5_PWM, LED4.anode
  N11: Componente1.D6_PWM, LED5.anode
  N12: Componente1.D7, LED6.anode
  N13: Componente1.5V, R2.leg2
  N14: R1.Pin_0, LED10.cathode
  N15: LED1.cathode, R4.Pin_0
  N16: LED2.cathode, R5.Pin_0
  N17: LED3.cathode, R6.Pin_0
  N18: LED4.cathode, R8.Pin_0
  N19: LED5.cathode, R11.Pin_0
  N20: LED6.cathode, R10.Pin_0
  N21: LED7.cathode, R9.Pin_0
  N22: LED8.cathode, R7.Pin_0
  N23: LED9.cathode, R3.Pin_0
