# Fritzing sketch project (saved by Fritzing 0.9.10b)
breadboards: 1

parts:
  Part1 = KY-037 High Sensitivity Sound Detection Module [package="Breakout board"]
  Componente1 = Arduino Uno (Rev3)
  LED1 = smd LED [color="White (4500K)" package="0805 [SMD]"]
  R1 = Resistor [tolerance=±5% resistance=220 package="2512 [SMD]"]

nets:
  N1: Part1.G, Componente1.GND, R1.Pin_0
  N2: Part1.+, Componente1.5V, LED1.anode
  N3: Part1.D0, Componente1.D7
  N4: LED1.cathode, R1.Pin_1

custom parts:
  KY-037 High Sensitivity Sound Detection Module: KY-037 high sensitivity sound detection module is an analog/digital sensor that uses a condenser microphone to observe changes in environment noise.
