# Fritzing sketch assembly-diagram (saved by Fritzing 0.9.10b)
breadboards: 1

parts:
  Componente1 = Arduino Uno (Rev3)
  U1 = Optocoupler [package=THT]
  R1 = Resistor [tolerance=±5% resistance=220 package="2010 [SMD]"]
  LED1 = smd LED [color="Orange (620nm)" package="0603 [SMD]"]
  R2 = Resistor [tolerance=±5% resistance=220 package="2010 [SMD]"]

nets:
  N1: Componente1.D7, R1.Pin_0
  N2: Componente1.5V, R2.Pin_0
  N3: Componente1.GND, U1.Pin_2, U1.Pin_4
  N4: U1.Pin_1, R1.Pin_1
  N5: U1.Pin_5, LED1.cathode
  N6: LED1.anode, R2.Pin_1
