# Fritzing sketch wiring-approx-diagram (saved by Fritzing 0.9.10b)
breadboards: 1

parts:
  part = DC Power [voltage=1.2V]
  part_2 = Resistor [tolerance=±5% resistance=10 package="0805 [SMD]"]
  Switch = SWITCH-SPST-2 [package=switch-spst-vertical]
  NPN = TRANSISTOR_NPN [package=to-92-ammo]
  part_3 = smd LED [color="Orange (620nm)" package="1206 [SMD]"]
  part_4 = Resistor [tolerance=±5% resistance=220 package="0805 [SMD]"]
  part_5 = DC Power [voltage=5V]

nets:
  N1: part.V+, part_2.Pin_0
  GND: part.V-, NPN.E, part_5.V-
  N2: part_2.Pin_1, Switch.P
  N3: Switch.O, NPN.B
  N4: NPN.C, part_3.cathode
  N5: part_3.anode, part_4.Pin_1
  N6: part_4.Pin_0, part_5.V+
