# Fritzing sketch wiring-diagram (saved by Fritzing 0.9.10b)
breadboards: 1

parts:
  Optocoupler = Optocoupler [package=THT]
  R1 = Resistor [tolerance=±5% resistance=220 package="2010 [SMD]"]
  LED1 = smd LED [color="Orange (620nm)" package="0603 [SMD]"]
  R2 = Resistor [tolerance=±5% resistance=220 package="2010 [SMD]"]
  Microcontroller = Arduino Uno (Rev3)

nets:
  N1: Optocoupler.Pin_1, R1.Pin_1
  N2: Optocoupler.Pin_2, Optocoupler.Pin_4, Microcontroller.GND
  N3: Optocoupler.Pin_5, LED1.cathode
  N4: R1.Pin_0, Microcontroller.D7
  N5: LED1.anode, R2.Pin_1
  N6: R2.Pin_0, Microcontroller.5V
